# Fritzing sketch ArbolNavidad (saved by Fritzing 0.8.3b)
breadboards: 1

parts:
  Parte1 = Arduino Uno (Rev3)
  U2 = 74HC595 [package="DIP16 [THT]"]
  R1 = Resistor [tolerance=±5% resistance=130 package=THT]
  LED1 = LED - 5mm [color="Red (633nm)" package="5 mm [THT]"]
  R2 = Resistor [tolerance=±5% resistance=130 package=THT]
  LED2 = LED - 5mm [color="Red (633nm)" package="5 mm [THT]"]
  R3 = Resistor [tolerance=±5% resistance=130 package=THT]
  LED3 = LED - 5mm [color="Red (633nm)" package="5 mm [THT]"]
  R4 = Resistor [tolerance=±5% resistance=130 package=THT]
  LED4 = LED - 5mm [color="Red (633nm)" package="5 mm [THT]"]
  R5 = Resistor [tolerance=±5% resistance=130 package=THT]
  LED5 = LED - 5mm [color="Red (633nm)" package="5 mm [THT]"]
  R6 = Resistor [tolerance=±5% resistance=130 package=THT]
  LED6 = LED - 5mm [color="Red (633nm)" package="5 mm [THT]"]
  R7 = Resistor [tolerance=±5% resistance=130 package=THT]
  LED7 = LED - 5mm [color="Red (633nm)" package="5 mm [THT]"]
  R8 = Resistor [tolerance=±5% resistance=130 package=THT]
  LED8 = LED - 5mm [color="Red (633nm)" package="5 mm [THT]"]
  U3 = 74HC595 [package="DIP16 [THT]"]
  R9 = Resistor [tolerance=±5% resistance=130 package=THT]
  R10 = Resistor [tolerance=±5% resistance=130 package=THT]
  R11 = Resistor [tolerance=±5% resistance=130 package=THT]
  R12 = Resistor [tolerance=±5% resistance=130 package=THT]
  R13 = Resistor [tolerance=±5% resistance=130 package=THT]
  R14 = Resistor [tolerance=±5% resistance=130 package=THT]
  R15 = Resistor [tolerance=±5% resistance=130 package=THT]
  R16 = Resistor [tolerance=±5% resistance=130 package=THT]
  LED9 = LED - 5mm [color="Red (633nm)" package="5 mm [THT]"]
  LED10 = LED - 5mm [color="Red (633nm)" package="5 mm [THT]"]
  LED11 = LED - 5mm [color="Red (633nm)" package="5 mm [THT]"]
  LED12 = LED - 5mm [color="Red (633nm)" package="5 mm [THT]"]
  LED13 = LED - 5mm [color="Red (633nm)" package="5 mm [THT]"]
  LED14 = LED - 5mm [color="Red (633nm)" package="5 mm [THT]"]
  LED15 = LED - 5mm [color="Red (633nm)" package="5 mm [THT]"]
  LED16 = LED - 5mm [color="Red (633nm)" package="5 mm [THT]"]
  U4 = 74HC595 [package="DIP16 [THT]"]
  U5 = 74HC595 [package="DIP16 [THT]"]
  R17 = Resistor [tolerance=±5% resistance=130 package=THT]
  R18 = Resistor [tolerance=±5% resistance=130 package=THT]
  R19 = Resistor [tolerance=±5% resistance=130 package=THT]
  R20 = Resistor [tolerance=±5% resistance=130 package=THT]
  R21 = Resistor [tolerance=±5% resistance=130 package=THT]
  R22 = Resistor [tolerance=±5% resistance=130 package=THT]
  R23 = Resistor [tolerance=±5% resistance=130 package=THT]
  R24 = Resistor [tolerance=±5% resistance=130 package=THT]
  R25 = Resistor [tolerance=±5% resistance=130 package=THT]
  R26 = Resistor [tolerance=±5% resistance=130 package=THT]
  R27 = Resistor [tolerance=±5% resistance=130 package=THT]
  R28 = Resistor [tolerance=±5% resistance=130 package=THT]
  R29 = Resistor [tolerance=±5% resistance=130 package=THT]
  R30 = Resistor [tolerance=±5% resistance=130 package=THT]
  R31 = Resistor [tolerance=±5% resistance=130 package=THT]
  R32 = Resistor [tolerance=±5% resistance=130 package=THT]
  LED17 = LED - 5mm [color="Red (633nm)" package="5 mm [THT]"]
  LED18 = LED - 5mm [color="Red (633nm)" package="5 mm [THT]"]
  LED19 = LED - 5mm [color="Red (633nm)" package="5 mm [THT]"]
  LED20 = LED - 5mm [color="Red (633nm)" package="5 mm [THT]"]
  LED21 = LED - 5mm [color="Red (633nm)" package="5 mm [THT]"]
  LED22 = LED - 5mm [color="Red (633nm)" package="5 mm [THT]"]
  LED23 = LED - 5mm [color="Red (633nm)" package="5 mm [THT]"]
  LED24 = LED - 5mm [color="Red (633nm)" package="5 mm [THT]"]
  LED25 = LED - 5mm [color="Red (633nm)" package="5 mm [THT]"]
  LED26 = LED - 5mm [color="Red (633nm)" package="5 mm [THT]"]
  LED27 = LED - 5mm [color="Red (633nm)" package="5 mm [THT]"]
  LED28 = LED - 5mm [color="Red (633nm)" package="5 mm [THT]"]
  LED29 = LED - 5mm [color="Red (633nm)" package="5 mm [THT]"]
  LED30 = LED - 5mm [color="Red (633nm)" package="5 mm [THT]"]
  LED31 = LED - 5mm [color="Red (633nm)" package="5 mm [THT]"]
  LED32 = LED - 5mm [color="Red (633nm)" package="5 mm [THT]"]

nets:
  N1: Parte1.ICSP_MISO, Parte1.D12/MISO, U2.ST_CP, U3.ST_CP, U4.ST_CP, U5.ST_CP
  5V: Parte1.5V, U2.MR, U2.VCC, U3.MR, U3.VCC, U4.MR, U4.VCC, U5.MR, U5.VCC
  N2: Parte1.ICSP_MOSI, Parte1.D11_PWM/MOSI, U3.DS
  GND: Parte1.GND, U2.GND, U2.OE, LED1.cathode, LED2.cathode, LED3.cathode, LED4.cathode, LED5.cathode, LED6.cathode, LED7.cathode, LED8.cathode, U3.GND, U3.OE, LED9.cathode, LED10.cathode, LED11.cathode, LED12.cathode, LED13.cathode, LED14.cathode, LED15.cathode, LED16.cathode, U4.GND, U4.OE, U5.GND, U5.OE, LED17.cathode, LED18.cathode, LED19.cathode, LED20.cathode, LED21.cathode, LED22.cathode, LED23.cathode, LED24.cathode, LED25.cathode, LED26.cathode, LED27.cathode, LED28.cathode, LED29.cathode, LED30.cathode, LED31.cathode, LED32.cathode
  N3: Parte1.D8, U2.SH_CP, U3.SH_CP, U4.SH_CP, U5.SH_CP
  N4: Parte1.D10_PWM/SS, U4.DS
  N5: U2.Q1, R1.Pin_0
  N6: U2.Q2, R2.Pin_0
  N7: U2.Q3, R4.Pin_0
  N8: U2.Q4, R5.Pin_0
  N9: U2.Q5, R6.Pin_0
  N10: U2.Q6, R7.Pin_0
  N11: U2.Q7, R8.Pin_0
  N12: U2.DS, U3.Q7'
  N13: U2.Q0, R3.Pin_0
  N14: R1.Pin_1, LED1.anode
  N15: R2.Pin_1, LED2.anode
  N16: R3.Pin_1, LED3.anode
  N17: R4.Pin_1, LED4.anode
  N18: R5.Pin_1, LED5.anode
  N19: R6.Pin_1, LED6.anode
  N20: R7.Pin_1, LED7.anode
  N21: R8.Pin_1, LED8.anode
  N22: U3.Q1, R14.Pin_0
  N23: U3.Q2, R12.Pin_0
  N24: U3.Q3, R9.Pin_0
  N25: U3.Q4, R11.Pin_0
  N26: U3.Q5, R15.Pin_0
  N27: U3.Q6, R10.Pin_0
  N28: U3.Q7, R13.Pin_0
  N29: U3.Q0, R16.Pin_0
  N30: R9.Pin_1, LED14.anode
  N31: R10.Pin_1, LED11.anode
  N32: R11.Pin_1, LED10.anode
  N33: R12.Pin_1, LED9.anode
  N34: R13.Pin_1, LED15.anode
  N35: R14.Pin_1, LED12.anode
  N36: R15.Pin_1, LED13.anode
  N37: R16.Pin_1, LED16.anode
  N38: U4.Q1, R27.Pin_0
  N39: U4.Q2, R26.Pin_0
  N40: U4.Q3, R25.Pin_0
  N41: U4.Q4, R30.Pin_0
  N42: U4.Q5, R32.Pin_0
  N43: U4.Q6, R31.Pin_0
  N44: U4.Q7, R24.Pin_0
  N45: U4.Q7', U5.DS
  N46: U4.Q0, R29.Pin_0
  N47: U5.Q1, R23.Pin_0
  N48: U5.Q2, R28.Pin_0
  N49: U5.Q3, R18.Pin_0
  N50: U5.Q4, R21.Pin_0
  N51: U5.Q5, R17.Pin_0
  N52: U5.Q6, R22.Pin_0
  N53: U5.Q7, R20.Pin_0
  N54: U5.Q0, R19.Pin_0
  N55: R17.Pin_1, LED19.anode
  N56: R18.Pin_1, LED26.anode
  N57: R19.Pin_1, LED17.anode
  N58: R20.Pin_1, LED23.anode
  N59: R21.Pin_1, LED18.anode
  N60: R22.Pin_1, LED30.anode
  N61: R23.Pin_1, LED29.anode
  N62: R24.Pin_1, LED28.anode
  N63: R25.Pin_1, LED22.anode
  N64: R26.Pin_1, LED32.anode
  N65: R27.Pin_1, LED20.anode
  N66: R28.Pin_1, LED21.anode
  N67: R29.Pin_1, LED24.anode
  N68: R30.Pin_1, LED31.anode
  N69: R31.Pin_1, LED27.anode
  N70: R32.Pin_1, LED25.anode
