# Fritzing sketch ArbolNavidadSimplificado (saved by Fritzing 0.9.0b)
circuit board: 6.60931cm x 8.15997cm
breadboards: 1

parts:
  U3 = 74HC595 [package="DIP16 [THT]"]
  R9 = Resistor [tolerance=±5% resistance=130 package=THT]
  R10 = Resistor [tolerance=±5% resistance=130 package=THT]
  R11 = Resistor [tolerance=±5% resistance=130 package=THT]
  R12 = Resistor [tolerance=±5% resistance=130 package=THT]
  R13 = Resistor [tolerance=±5% resistance=130 package=THT]
  R14 = Resistor [tolerance=±5% resistance=130 package=THT]
  R15 = Resistor [tolerance=±5% resistance=130 package=THT]
  R16 = Resistor [tolerance=±5% resistance=130 package=THT]
  LED9 = LED - 5mm [color="Red (633nm)" package="5 mm [THT]"]
  LED10 = LED - 5mm [color="Red (633nm)" package="5 mm [THT]"]
  LED11 = LED - 5mm [color="Red (633nm)" package="5 mm [THT]"]
  LED12 = LED - 5mm [color="Red (633nm)" package="5 mm [THT]"]
  LED13 = LED - 5mm [color="Red (633nm)" package="5 mm [THT]"]
  LED14 = LED - 5mm [color="Red (633nm)" package="5 mm [THT]"]
  LED15 = LED - 5mm [color="Red (633nm)" package="5 mm [THT]"]
  LED16 = LED - 5mm [color="Red (633nm)" package="5 mm [THT]"]
  U4 = 74HC595 [package="DIP16 [THT]"]
  R24 = Resistor [tolerance=±5% resistance=130 package=THT]
  R25 = Resistor [tolerance=±5% resistance=130 package=THT]
  R26 = Resistor [tolerance=±5% resistance=130 package=THT]
  R27 = Resistor [tolerance=±5% resistance=130 package=THT]
  R30 = Resistor [tolerance=±5% resistance=130 package=THT]
  R31 = Resistor [tolerance=±5% resistance=130 package=THT]
  R32 = Resistor [tolerance=±5% resistance=130 package=THT]
  LED20 = LED - 5mm [color="Red (633nm)" package="5 mm [THT]"]
  LED22 = LED - 5mm [color="Red (633nm)" package="5 mm [THT]"]
  LED24 = LED - 5mm [color="Red (633nm)" package="5 mm [THT]"]
  LED25 = LED - 5mm [color="Red (633nm)" package="5 mm [THT]"]
  LED27 = LED - 5mm [color="Red (633nm)" package="5 mm [THT]"]
  LED28 = LED - 5mm [color="Red (633nm)" package="5 mm [THT]"]
  LED31 = LED - 5mm [color="Red (633nm)" package="5 mm [THT]"]
  LED32 = LED - 5mm [color="Red (633nm)" package="5 mm [THT]"]
  Parte1 = Arduino Uno (Rev3)
  R33 = Resistor [tolerance=±5% resistance=130 package=THT]

nets:
  N1: U3.Q1, R14.Pin_0
  N2: U3.Q2, R12.Pin_0
  N3: U3.Q3, R9.Pin_0
  N4: U3.Q4, R11.Pin_0
  N5: U3.Q5, R15.Pin_0
  N6: U3.Q6, R10.Pin_0
  N7: U3.Q7, R13.Pin_0
  GND: U3.GND, U3.OE, LED9.cathode, LED10.cathode, LED11.cathode, LED12.cathode, LED13.cathode, LED14.cathode, LED15.cathode, LED16.cathode, U4.GND, U4.OE, LED20.cathode, LED22.cathode, LED24.cathode, LED25.cathode, LED27.cathode, LED28.cathode, LED31.cathode, LED32.cathode, Parte1.GND
  5V: U3.MR, U3.VCC, U4.MR, U4.VCC, Parte1.5V
  N8: U3.SH_CP, U4.SH_CP, Parte1.D8
  N9: U3.ST_CP, U4.ST_CP, Parte1.D12/MISO
  N10: U3.DS, Parte1.D11_PWM/MOSI
  N11: U3.Q0, R16.Pin_0
  N12: R9.Pin_1, LED14.anode
  N13: R10.Pin_1, LED11.anode
  N14: R11.Pin_1, LED10.anode
  N15: R12.Pin_1, LED9.anode
  N16: R13.Pin_1, LED15.anode
  N17: R14.Pin_1, LED12.anode
  N18: R15.Pin_1, LED13.anode
  N19: R16.Pin_1, LED16.anode
  N20: U4.Q1, R27.Pin_0
  N21: U4.Q2, R26.Pin_0
  N22: U4.Q3, R25.Pin_0
  N23: U4.Q4, R30.Pin_0
  N24: U4.Q5, R32.Pin_0
  N25: U4.Q6, R31.Pin_0
  N26: U4.Q7, R24.Pin_0
  N27: U4.DS, Parte1.D10_PWM/SS
  N28: U4.Q0, R33.Pin_0
  N29: R24.Pin_1, LED28.anode
  N30: R25.Pin_1, LED22.anode
  N31: R26.Pin_1, LED32.anode
  N32: R27.Pin_1, LED20.anode
  N33: R30.Pin_1, LED31.anode
  N34: R31.Pin_1, LED27.anode
  N35: R32.Pin_1, LED25.anode
  N36: LED24.anode, R33.Pin_1
