# Fritzing sketch Modulo2_595_Paralelo (saved by Fritzing 0.9.0b)
circuit board: 4.40806cm x 5.55285cm
breadboards: 1

parts:
  U3 = 74HC595 [package="DIP16 [THT]"]
  R9 = Resistor [tolerance=±5% resistance=130 package=THT]
  R10 = Resistor [tolerance=±5% resistance=130 package=THT]
  R11 = Resistor [tolerance=±5% resistance=130 package=THT]
  R12 = Resistor [tolerance=±5% resistance=130 package=THT]
  R13 = Resistor [tolerance=±5% resistance=130 package=THT]
  R14 = Resistor [tolerance=±5% resistance=130 package=THT]
  R15 = Resistor [tolerance=±5% resistance=130 package=THT]
  R16 = Resistor [tolerance=±5% resistance=130 package=THT]
  U4 = 74HC595 [package="DIP16 [THT]"]
  R24 = Resistor [tolerance=±5% resistance=130 package=THT]
  R25 = Resistor [tolerance=±5% resistance=130 package=THT]
  R26 = Resistor [tolerance=±5% resistance=130 package=THT]
  R27 = Resistor [tolerance=±5% resistance=130 package=THT]
  R30 = Resistor [tolerance=±5% resistance=130 package=THT]
  R31 = Resistor [tolerance=±5% resistance=130 package=THT]
  R32 = Resistor [tolerance=±5% resistance=130 package=THT]
  J1 = male pin header, 4 pins [form="♂ (male)"]
  J2 = male pin header, 2 pins [form="♂ (male)"]
  J5 = double row male pin header, 16 pins [form="♂ (male)"]
  J3 = female pin header, 2 pins [form="♀ (female)"]
  J7 = female pin header, 4 pins [form="♀ (female)"]
  R33 = Resistor [tolerance=±5% resistance=130 package=THT]
  J6 = double row male pin header, 16 pins [form="♂ (male)"]

nets:
  N1: U3.Q1, R14.Pin_0
  N2: U3.Q2, R12.Pin_0
  N3: U3.Q3, R9.Pin_0
  N4: U3.Q4, R11.Pin_0
  N5: U3.Q5, R15.Pin_0
  N6: U3.Q6, R10.Pin_0
  N7: U3.Q7, R13.Pin_0
  GND: U3.GND, U3.OE, U4.GND, U4.OE, J2.pin1, J5.pin1, J5.pin2, J5.pin3, J5.pin4, J5.pin5, J5.pin6, J5.pin7, J5.pin8, J3.pin1, J6.pin1, J6.pin2, J6.pin3, J6.pin4, J6.pin5, J6.pin6, J6.pin7, J6.pin8
  N8: U3.Q7', J7.pin3
  5V: U3.MR, U3.VCC, U4.MR, U4.VCC, J2.pin2, J3.pin2
  N9: U3.SH_CP, U4.SH_CP, J1.pin1, J7.pin1
  N10: U3.ST_CP, U4.ST_CP, J1.pin4, J7.pin4
  N11: U3.DS, J1.pin3
  N12: U3.Q0, R16.Pin_0
  N13: R9.Pin_1, J6.pin13
  N14: R10.Pin_1, J6.pin10
  N15: R11.Pin_1, J6.pin12
  N16: R12.Pin_1, J6.pin14
  N17: R13.Pin_1, J6.pin9
  N18: R14.Pin_1, J6.pin15
  N19: R15.Pin_1, J6.pin11
  N20: R16.Pin_1, J6.pin16
  N21: U4.Q1, R27.Pin_0
  N22: U4.Q2, R26.Pin_0
  N23: U4.Q3, R25.Pin_0
  N24: U4.Q4, R30.Pin_0
  N25: U4.Q5, R32.Pin_0
  N26: U4.Q6, R31.Pin_0
  N27: U4.Q7, R24.Pin_0
  N28: U4.Q7', J7.pin2
  N29: U4.DS, J1.pin2
  N30: U4.Q0, R33.Pin_0
  N31: R24.Pin_1, J5.pin9
  N32: R25.Pin_1, J5.pin13
  N33: R26.Pin_1, J5.pin14
  N34: R27.Pin_1, J5.pin15
  N35: R30.Pin_1, J5.pin12
  N36: R31.Pin_1, J5.pin10
  N37: R32.Pin_1, J5.pin11
  N38: J5.pin16, R33.Pin_1

notes:
  In
  Out
