# Fritzing sketch Modulo_2x2_595 (saved by Fritzing 0.9.0b)
circuit board: 7.87619cm x 6.36207cm
breadboards: 1

parts:
  U2 = 74HC595 [package="DIP16 [THT]"]
  R1 = Resistor [tolerance=±5% resistance=220k package=THT]
  R2 = Resistor [tolerance=±5% resistance=130 package=THT]
  R3 = Resistor [tolerance=±5% resistance=130 package=THT]
  R4 = Resistor [tolerance=±5% resistance=130 package=THT]
  R5 = Resistor [tolerance=±5% resistance=130 package=THT]
  R6 = Resistor [tolerance=±5% resistance=130 package=THT]
  R7 = Resistor [tolerance=±5% resistance=130 package=THT]
  R8 = Resistor [tolerance=±5% resistance=130 package=THT]
  U3 = 74HC595 [package="DIP16 [THT]"]
  R9 = Resistor [tolerance=±5% resistance=130 package=THT]
  R10 = Resistor [tolerance=±5% resistance=130 package=THT]
  R11 = Resistor [tolerance=±5% resistance=130 package=THT]
  R12 = Resistor [tolerance=±5% resistance=130 package=THT]
  R13 = Resistor [tolerance=±5% resistance=130 package=THT]
  R14 = Resistor [tolerance=±5% resistance=130 package=THT]
  R15 = Resistor [tolerance=±5% resistance=130 package=THT]
  R16 = Resistor [tolerance=±5% resistance=130 package=THT]
  U4 = 74HC595 [package="DIP16 [THT]"]
  U5 = 74HC595 [package="DIP16 [THT]"]
  R17 = Resistor [tolerance=±5% resistance=130 package=THT]
  R18 = Resistor [tolerance=±5% resistance=130 package=THT]
  R19 = Resistor [tolerance=±5% resistance=130 package=THT]
  R21 = Resistor [tolerance=±5% resistance=130 package=THT]
  R22 = Resistor [tolerance=±5% resistance=130 package=THT]
  R23 = Resistor [tolerance=±5% resistance=130 package=THT]
  R24 = Resistor [tolerance=±5% resistance=130 package=THT]
  R25 = Resistor [tolerance=±5% resistance=130 package=THT]
  R26 = Resistor [tolerance=±5% resistance=130 package=THT]
  R27 = Resistor [tolerance=±5% resistance=130 package=THT]
  R28 = Resistor [tolerance=±5% resistance=130 package=THT]
  R30 = Resistor [tolerance=±5% resistance=130 package=THT]
  R31 = Resistor [tolerance=±5% resistance=130 package=THT]
  R32 = Resistor [tolerance=±5% resistance=130 package=THT]
  R33 = Resistor [tolerance=±5% resistance=130 package=THT]
  R34 = Resistor [tolerance=±5% resistance=130 package=THT]
  J1 = male pin header, 4 pins [form="♂ (male)"]
  J2 = male pin header, 2 pins [form="♂ (male)"]
  J3 = female pin header, 4 pins [form="♀ (female)"]
  J4 = female pin header, 2 pins [form="♀ (female)"]
  J5 = double row male pin header, 16 pins [form="♂ (male)"]
  J6 = double row male pin header, 16 pins [form="♂ (male)"]
  J7 = double row male pin header, 16 pins [form="♂ (male)"]
  J8 = double row male pin header, 16 pins [form="♂ (male)"]

nets:
  N1: U2.Q1, R1.Pin_0
  N2: U2.Q2, R2.Pin_0
  N3: U2.Q3, R4.Pin_0
  N4: U2.Q4, R5.Pin_0
  N5: U2.Q5, R6.Pin_0
  N6: U2.Q6, R7.Pin_0
  N7: U2.Q7, R8.Pin_0
  GND: U2.GND, U2.OE, U3.GND, U3.OE, U4.GND, U4.OE, U5.GND, U5.OE, J2.pin2, J4.pin2, J5.pin1, J5.pin2, J5.pin3, J5.pin4, J5.pin5, J5.pin6, J5.pin7, J5.pin8, J6.pin1, J6.pin2, J6.pin3, J6.pin4, J6.pin5, J6.pin6, J6.pin7, J6.pin8, J7.pin1, J7.pin2, J7.pin3, J7.pin4, J7.pin5, J7.pin6, J7.pin7, J7.pin8, J8.pin1, J8.pin2, J8.pin3, J8.pin4, J8.pin5, J8.pin6, J8.pin7, J8.pin8
  N8: U2.Q7', J3.pin3
  5V: U2.MR, U2.VCC, U3.MR, U3.VCC, U4.MR, U4.VCC, U5.MR, U5.VCC, J2.pin1, J4.pin1
  N9: U2.SH_CP, U3.SH_CP, U4.SH_CP, U5.SH_CP, J1.pin1, J3.pin1
  N10: U2.ST_CP, U3.ST_CP, U4.ST_CP, U5.ST_CP, J1.pin4, J3.pin4
  N11: U2.DS, U3.Q7'
  N12: U2.Q0, R3.Pin_0
  N13: R1.Pin_1, J7.pin15
  N14: R2.Pin_1, J7.pin14
  N15: R3.Pin_1, J7.pin16
  N16: R4.Pin_1, J7.pin13
  N17: R5.Pin_1, J7.pin12
  N18: R6.Pin_1, J7.pin11
  N19: R7.Pin_1, J7.pin10
  N20: R8.Pin_1, J7.pin9
  N21: U3.Q1, R14.Pin_0
  N22: U3.Q2, R12.Pin_0
  N23: U3.Q3, R9.Pin_0
  N24: U3.Q4, R11.Pin_0
  N25: U3.Q5, R15.Pin_0
  N26: U3.Q6, R10.Pin_0
  N27: U3.Q7, R13.Pin_0
  N28: U3.DS, J1.pin3
  N29: U3.Q0, R16.Pin_0
  N30: R9.Pin_1, J8.pin13
  N31: R10.Pin_1, J8.pin10
  N32: R11.Pin_1, J8.pin12
  N33: R12.Pin_1, J8.pin14
  N34: R13.Pin_1, J8.pin9
  N35: R14.Pin_1, J8.pin15
  N36: R15.Pin_1, J8.pin11
  N37: R16.Pin_1, J8.pin16
  N38: U4.Q1, R27.Pin_0
  N39: U4.Q2, R26.Pin_0
  N40: U4.Q3, R25.Pin_0
  N41: U4.Q4, R30.Pin_0
  N42: U4.Q5, R32.Pin_0
  N43: U4.Q6, R31.Pin_0
  N44: U4.Q7, R24.Pin_0
  N45: U4.Q7', U5.DS
  N46: U4.DS, J1.pin2
  N47: U4.Q0, R33.Pin_0
  N48: U5.Q1, R23.Pin_0
  N49: U5.Q2, R28.Pin_0
  N50: U5.Q3, R18.Pin_0
  N51: U5.Q4, R21.Pin_0
  N52: U5.Q5, R17.Pin_0
  N53: U5.Q6, R22.Pin_0
  N54: U5.Q7, R34.Pin_0
  N55: U5.Q7', J3.pin2
  N56: U5.Q0, R19.Pin_0
  N57: R17.Pin_1, J6.pin11
  N58: R18.Pin_1, J6.pin13
  N59: R19.Pin_1, J6.pin16
  N60: R21.Pin_1, J6.pin12
  N61: R22.Pin_1, J6.pin10
  N62: R23.Pin_1, J6.pin15
  N63: R24.Pin_1, J5.pin9
  N64: R25.Pin_1, J5.pin13
  N65: R26.Pin_1, J5.pin14
  N66: R27.Pin_1, J5.pin15
  N67: R28.Pin_1, J6.pin14
  N68: R30.Pin_1, J5.pin12
  N69: R31.Pin_1, J5.pin10
  N70: R32.Pin_1, J5.pin11
  N71: R33.Pin_1, J5.pin16
  N72: R34.Pin_1, J6.pin9
