# Fritzing sketch Bt_hc_06 (saved by Fritzing 0.9.0b)
breadboards: 1

parts:
  Parte1 = JY-MCU
  Parte2 = Arduino Uno (Rev3)
  LED1 = RGB LED (com. cathode, rbg) [package="5 mm [THT]"]
  R1 = Resistor [tolerance=±5% resistance=220 package=THT]
  R2 = Resistor [tolerance=±5% resistance=220 package=THT]
  R3 = Resistor [tolerance=±5% resistance=220 package=THT]

nets:
  N1: Parte1.TX, Parte2.D12/MISO
  5V: Parte1.VCC, Parte2.5V
  N2: Parte1.RX, Parte2.D13/SCK
  GND: Parte1.GND, Parte2.GND, LED1.common_cathode
  N3: Parte2.D3_PWM, R3.Pin_0
  N4: Parte2.D5_PWM, R2.Pin_0
  N5: Parte2.D6_PWM, R1.Pin_0
  N6: LED1.red_anode, R1.Pin_1
  N7: LED1.blue_anode, R2.Pin_1
  N8: LED1.green_anode, R3.Pin_1

custom parts:
  JY-MCU: Description: The Bluetooth Mate is very similar to our BlueSMiRF modem, but it is designed specifically to be used with our Arduino Pros and LilyPad Arduinos. These modems work as a serial (RX/TX) pipe, and are a great wireless replacement for serial cables. Any serial stream from 9600 to 115200bps can be passed seamlessly from your computer to your target. Bluetooth Mate has the same pin out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
