# Fritzing sketch Test74HC597 (saved by Fritzing 0.9.0b)
breadboards: 2

parts:
  Parte1 = Arduino Uno (Rev3)
  U1 = 74HC595 [package="DIP16 [THT]"]
  R1 = Resistor [tolerance=±5% resistance=10k package=THT]
  R3 = Resistor [tolerance=±5% resistance=10k package=THT]
  R4 = Resistor [tolerance=±5% resistance=10k package=THT]
  R5 = Resistor [tolerance=±5% resistance=10k package=THT]
  R2 = Resistor [tolerance=±5% resistance=10k package=THT]
  R6 = Resistor [tolerance=±5% resistance=10k package=THT]
  R7 = Resistor [tolerance=±5% resistance=10k package=THT]
  R8 = Resistor [tolerance=±5% resistance=10k package=THT]
  S1 = Momentary Switch [package=ksa_sealed_tac_switch]
  S2 = Momentary Switch [package=ksa_sealed_tac_switch]
  S3 = Momentary Switch [package=ksa_sealed_tac_switch]
  S4 = Momentary Switch [package=ksa_sealed_tac_switch]
  S5 = Momentary Switch [package=ksa_sealed_tac_switch]
  S6 = Momentary Switch [package=ksa_sealed_tac_switch]
  S7 = Momentary Switch [package=ksa_sealed_tac_switch]
  S8 = Momentary Switch [package=ksa_sealed_tac_switch]

nets:
  N1: Parte1.D8, U1.OE
  N2: Parte1.D9_PWM, U1.ST_CP
  N3: Parte1.D10_PWM/SS, U1.SH_CP
  N4: Parte1.D11_PWM/MOSI, U1.Q7'
  GND: Parte1.GND, U1.GND, R1.Pin_0, R3.Pin_1, R4.Pin_1, R5.Pin_1, R2.Pin_1, R6.Pin_1, R7.Pin_1, R8.Pin_1
  5V: Parte1.5V, U1.MR, U1.VCC, S1.2, S2.2, S3.2, S4.2, S5.2, S6.2, S7.2, S8.2
  N5: U1.Q1, R5.Pin_0, S1.3
  N6: U1.Q2, R4.Pin_0, S7.3
  N7: U1.Q3, R3.Pin_0, S5.3
  N8: U1.Q4, R2.Pin_0, S4.3
  N9: U1.Q5, R6.Pin_0, S3.3
  N10: U1.Q6, R8.Pin_0, S2.3
  N11: U1.Q7, R7.Pin_0, S8.3
  N12: U1.Q0, R1.Pin_1, S6.3
